// Digital circuit Main.dig as structural Verilog
module Main (
);

  Memory memory_1 ();  // open: ADDR, Control, MEM
  Memory_Bridge memory_bridge_1 ();  // open: MAIN, MEM, Control
  Tranfer_Register tranfer_register_1 ();  // open: MAIN, XFER, ADDR, Control
  GPR gpr_1 ();  // open: RHS, LHS, MAIN, Control, I
  Constant_Register constant_register_1 ();  // open: Control, MEM, MAIN, I
  Address_Register address_register_1 ();  // open: XFER, ADDR, Control
  ALU alu_1 ();  // open: RHS, LHS, MAIN, FLAGS, Clock, Control
endmodule
